# Fritzing sketch Arduino (saved by Fritzing 0.9.2b)
circuit board: 8.46667cm x 5.64444cm
breadboards: 1

parts:
  Part1 = Arduino Nano (Rev3.0) (ICSP)
  S1 = Pushbutton [package="[SMD]"]
  R2 = Resistor [tolerance=±5% resistance=220 package="0402 [SMD]"]
  R3 = Resistor [tolerance=±5% resistance=220 package="0402 [SMD]"]
  Part3 = Bluetooth Mate Silver
  S2 = Pushbutton [package="[SMD]"]

nets (from the schematic view):
  N1: Part1.D0/RX, Part3.CTS_5V
  N2: Part1.GND, Part1.D2, Part1.D3, R2.Pin_0, R2.Pin_1, R3.Pin_0, Part3.RX_5V, Part3.TX_5V, S2.Pin_3, S2.Pin_4
  N3: S1.Pin_1, S1.Pin_2
  N4: S1.Pin_3, S1.Pin_4
  N5: S2.Pin_1, S2.Pin_2
